// Logisim project control_logic.circ as structural Verilog: 1 circuit, main circuit control_logic
module control_logic (
  input  [31:0] inst,
  input  BrEq,
  input  BrLt,
  input  in_4,
  output PCSel,
  output RegWEn,
  output [2:0] ImmSel,
  output BrUn,
  output ASel,
  output BSel,
  output [3:0] ALUSel,
  output MemRW,
  output [1:0] WBSel,
  output out_14,
  output out_15
);

  wire and_2_out, and_3_out, and_4_out, and_5_out, and_6_out, and_9_out, and_10_out, and_11_out, and_13_out,
       comparator_1_eq, comparator_2_eq, comparator_3_eq, comparator_4_eq, comparator_5_eq, comparator_6_eq,
       comparator_16_eq, comparator_16_gt, comparator_17_gt, I_type, is_sra, multiplexer_6_out, not_1_out,
       not_2_out, op_0x03, op_0x13, op_0x17, op_0x37, op_0x067, or_3_out, or_4_out, or_5_out, or_8_out,
       or_9_out, priority_encoder_1_gs, R_type, S_type, SB_type, U_type, UJ_type;
  wire [3:0] multiplexer_1_out, multiplexer_2_out, multiplexer_3_out, multiplexer_4_out,
       priority_encoder_1_out;

  Comparator #(.width(7), .mode("unsigned")) comparator_1 (
    .a(inst[31:25]), .b(7'b0000001), .eq(comparator_1_eq));  // open: gt, lt
  Comparator #(.width(7), .mode("unsigned")) comparator_2 (
    .a(inst[31:25]), .b(7'b0100000), .eq(comparator_2_eq));  // open: gt, lt
  Comparator #(.width(3), .mode("unsigned")) comparator_3 (
    .a(inst[14:12]), .b(3'b000), .eq(comparator_3_eq));  // open: gt, lt
  Comparator #(.width(3), .mode("unsigned")) comparator_4 (
    .a(inst[14:12]), .b(3'b101), .eq(comparator_4_eq));  // open: gt, lt
  Comparator #(.width(3), .mode("unsigned")) comparator_5 (
    .a(inst[14:12]), .b(3'b111), .eq(comparator_5_eq));  // open: gt, lt
  Comparator #(.width(3), .mode("unsigned")) comparator_6 (
    .a(inst[14:12]), .b(3'b001), .eq(comparator_6_eq));  // open: gt, lt
  Multiplexer #(.select(3), .width(4), .enable("false")) multiplexer_1 (
    .in0(4'b0000), .in1(4'b0110), .in2(4'b0111), .in3(4'b1011), .in4(4'b0011), .in5(4'b0100), .in6(4'b0010),
    .in7(4'b0001), .out(multiplexer_1_out), .sel(inst[14:12]));
  and and_1 (is_sra, comparator_2_eq, comparator_4_eq);
  and and_2 (and_2_out, comparator_1_eq, comparator_4_eq);
  and and_3 (and_3_out, comparator_1_eq, comparator_5_eq);
  and and_4 (and_4_out, comparator_3_eq, comparator_1_eq);
  and and_5 (and_5_out, comparator_3_eq, comparator_2_eq);
  and and_6 (and_6_out, comparator_1_eq, comparator_6_eq);
  Comparator #(.width(7), .mode("unsigned")) comparator_7 (.a(inst[6:0]), .b(7'b0110011), .eq(R_type));  // open: gt, lt
  Comparator #(.width(7), .mode("unsigned")) comparator_8 (
    .a(inst[6:0]), .b(7'b0000011), .eq(op_0x03));  // open: gt, lt
  Comparator #(.width(7), .mode("unsigned")) comparator_9 (
    .a(inst[6:0]), .b(7'b0010011), .eq(op_0x13));  // open: gt, lt
  Comparator #(.width(7), .mode("unsigned")) comparator_10 (
    .a(inst[6:0]), .b(7'b0100011), .eq(S_type));  // open: gt, lt
  Comparator #(.width(7), .mode("unsigned")) comparator_11 (
    .a(inst[6:0]), .b(7'b1100011), .eq(SB_type));  // open: gt, lt
  Comparator #(.width(7), .mode("unsigned")) comparator_12 (
    .a(inst[6:0]), .b(7'b0010111), .eq(op_0x17));  // open: gt, lt
  Comparator #(.width(7), .mode("unsigned")) comparator_13 (
    .a(inst[6:0]), .b(7'b0110111), .eq(op_0x37));  // open: gt, lt
  Comparator #(.width(7), .mode("unsigned")) comparator_14 (
    .a(inst[6:0]), .b(7'b1101111), .eq(UJ_type));  // open: gt, lt
  and and_7 (out_15, comparator_6_eq, op_0x03);
  and and_8 (out_14, comparator_3_eq, op_0x03);
  Comparator #(.width(7), .mode("unsigned")) comparator_15 (
    .a(inst[6:0]), .b(7'b1100111), .eq(op_0x067));  // open: gt, lt
  or or_1 (U_type, op_0x17, op_0x37);
  and and_9 (and_9_out, priority_encoder_1_gs, R_type);
  Priority_Encoder #(.select(4)) priority_encoder_1 (
    .in8(and_2_out), .in9(and_3_out), .in10(and_4_out), .in12(and_5_out), .in14(and_6_out),
    .out(priority_encoder_1_out), .gs(priority_encoder_1_gs));  // open: in0, in1, in2, in3, in4, in5, in6, in7, in11, in13, in15, en_out, en_in
  or or_2 (I_type, op_0x03, op_0x067, op_0x13);
  Multiplexer #(.width(4), .enable("false")) multiplexer_2 (
    .in0(multiplexer_1_out), .in1(priority_encoder_1_out), .out(multiplexer_2_out), .sel(and_9_out));
  Multiplexer #(.width(4), .enable("false")) multiplexer_3 (
    .in0(multiplexer_2_out), .in1(4'b0101), .out(multiplexer_3_out), .sel(is_sra));
  Multiplexer #(.width(4), .enable("false")) multiplexer_4 (
    .in0(4'b0000), .in1(multiplexer_3_out), .out(multiplexer_4_out), .sel(or_3_out));
  or or_3 (or_3_out, R_type, op_0x13);
  or or_4 (or_4_out, and_10_out, op_0x37);
  and and_10 (and_10_out, in_4, comparator_5_eq, S_type);
  Multiplexer #(.width(4), .enable("false")) multiplexer_5 (
    .in0(multiplexer_4_out), .in1(4'b1101), .out(ALUSel), .sel(or_4_out));
  not not_1 (not_1_out, BrEq);
  not not_2 (not_2_out, BrLt);
  or or_5 (or_5_out, R_type, op_0x13, U_type);
  Comparator #(.width(3), .mode("unsigned")) comparator_16 (
    .a(inst[14:12]), .b(3'b010), .gt(comparator_16_gt), .eq(comparator_16_eq));  // open: lt
  Comparator #(.width(3), .mode("unsigned")) comparator_17 (
    .a(inst[14:12]), .b(3'b101), .gt(comparator_17_gt));  // open: eq, lt
  Multiplexer #(.select(3), .enable("false")) multiplexer_6 (
    .in0(BrEq), .in1(not_1_out), .in4(BrLt), .in5(not_2_out), .in6(BrLt), .in7(not_2_out),
    .out(multiplexer_6_out), .sel(inst[14:12]));  // open: in2, in3
  Priority_Encoder priority_encoder_2 (
    .in0(I_type), .in1(S_type), .in2(SB_type), .in3(U_type), .in4(UJ_type), .out(ImmSel));  // open: in5, in6, in7, en_in, gs, en_out
  or or_6 (RegWEn, I_type, R_type, U_type, UJ_type);
  or or_7 (ASel, SB_type, U_type, UJ_type);
  not not_3 (BSel, R_type);
  or or_8 (or_8_out, op_0x067, UJ_type);
  and and_11 (and_11_out, in_4, comparator_16_gt);
  Priority_Encoder #(.select(2)) priority_encoder_3 (
    .in0(or_8_out), .in1(or_5_out), .in2(op_0x03), .out(WBSel));  // open: in3, gs, en_out, en_in
  or or_9 (or_9_out, and_11_out, comparator_16_eq);
  and and_12 (BrUn, comparator_17_gt, SB_type);
  and and_13 (and_13_out, multiplexer_6_out, SB_type);
  and and_14 (MemRW, or_9_out, S_type);
  or or_10 (PCSel, UJ_type, op_0x067, and_13_out);

  // Other names for the same wires on the sheet: opcode[6:0] = inst[6:0]; funct3[2:0] = inst[14:12];
  //   funct7[6:0] = inst[31:25]; LB = out_14; LH = out_15; swlt = in_4

  // Notes on the sheet:
  //   INPUTS to your circuit
  //   DON'T CHANGE THE LOCATIONS OF THE INPUTS AND OUTPUTS!
  //   OUTPUT from your circuit
endmodule
