// Logisim project cpu.circ as structural Verilog: 2 circuits, main circuit main
module main (
  input  [31:0] INSTRUCTION,
  input  in_2,
  output [31:0] PROGRAM_COUNTER,
  output [31:0] ra,
  output [31:0] sp,
  output [31:0] t0,
  output [31:0] t1,
  output [31:0] t2,
  output [31:0] s0,
  output [31:0] s1,
  output [31:0] a0
);

  wire branch_comp_1_breq, branch_comp_1_brlt, control_logic_1_asel, control_logic_1_brun,
       control_logic_1_bsel, control_logic_1_memrw, control_logic_1_out_14, control_logic_1_out_15,
       control_logic_1_regwen, PCSel, register_2_q, swlt_1_out_3;
  wire [1:0] control_logic_1_wbsel;
  wire [2:0] control_logic_1_immsel;
  wire [3:0] control_logic_1_alusel;
  wire [4:0] rd, rs1, rs2;
  wire [31:0] adder_1_out, Arithmetic_Logic_Unit_result, bit_extender_1_out, bit_extender_2_out, DMEM_p5,
       imm, multiplexer_1_out, multiplexer_2_out, multiplexer_3_out, multiplexer_4_out, multiplexer_5_out,
       multiplexer_6_out, RegFile_read_data_1, RegFile_read_data_2, register_1_q, register_3_q, wb;

  Adder #(.width(32)) adder_1 (.a(PROGRAM_COUNTER), .b(32'h4), .out(adder_1_out));  // open: cin, cout
  Multiplexer #(.width(32), .enable("false")) multiplexer_1 (
    .in0(adder_1_out), .in1(Arithmetic_Logic_Unit_result), .out(multiplexer_1_out), .sel(PCSel));
  Register #(.width(32)) PC (.D(multiplexer_1_out), .clk(in_2), .Q(PROGRAM_COUNTER));  // open: en, clr
  Register #(.width(32)) register_1 (.D(INSTRUCTION), .clk(in_2), .Q(register_1_q));  // open: en, clr
  Register #(.width(1)) register_2 (.D(PCSel), .clk(in_2), .Q(register_2_q));  // open: en, clr
  control_logic control_logic_1 (
    .ASel(control_logic_1_asel), .ImmSel(control_logic_1_immsel), .PCSel(PCSel),
    .RegWEn(control_logic_1_regwen), .BrUn(control_logic_1_brun), .BSel(control_logic_1_bsel),
    .BrLt(branch_comp_1_brlt), .BrEq(branch_comp_1_breq),
    .inst({multiplexer_2_out[31:25], rs2, rs1, multiplexer_2_out[14:12], rd, multiplexer_2_out[6:0]}),
    .ALUSel(control_logic_1_alusel), .MemRW(control_logic_1_memrw), .WBSel(control_logic_1_wbsel),
    .in_4(swlt_1_out_3), .out_14(control_logic_1_out_14), .out_15(control_logic_1_out_15));
  Register #(.width(32)) register_3 (.D(PROGRAM_COUNTER), .clk(in_2), .Q(register_3_q));  // open: en, clr
  Multiplexer #(.width(32), .enable("false")) multiplexer_2 (
    .in0(register_1_q), .in1(32'h13),
    .out({multiplexer_2_out[31:25], rs2, rs1, multiplexer_2_out[14:12], rd, multiplexer_2_out[6:0]}),
    .sel(register_2_q));
  imm_gen imm_gen_1 (
    .ImmSel(control_logic_1_immsel),
    .inst({multiplexer_2_out[31:25], rs2, rs1, multiplexer_2_out[14:12], rd, multiplexer_2_out[6:0]}),
    .imm(imm));
  regfile_main RegFile (
    .rs2(rs2), .rd(rd), .Read_Data_1(RegFile_read_data_1), .Read_Data_2(RegFile_read_data_2), .ra(ra),
    .sp(sp), .t0(t0), .t1(t1), .t2(t2), .s0(s0), .s1(s1), .a0(a0), .rs1(rs1), .Write_Data(wb),
    .RegWEn(control_logic_1_regwen), .clk(in_2));
  swlt swlt_1 (.in_1(RegFile_read_data_2), .in_2(imm), .out_3(swlt_1_out_3));
  Multiplexer #(.width(32), .enable("false")) multiplexer_3 (
    .in0(RegFile_read_data_1), .in1(register_3_q), .out(multiplexer_3_out), .sel(control_logic_1_asel));
  Multiplexer #(.width(32), .enable("false")) multiplexer_4 (
    .in0(RegFile_read_data_2), .in1(imm), .out(multiplexer_4_out), .sel(control_logic_1_bsel));
  branch_comp branch_comp_1 (
    .BrEq(branch_comp_1_breq), .BrUn(control_logic_1_brun), .rs1(RegFile_read_data_1),
    .BrLt(branch_comp_1_brlt), .rs2(RegFile_read_data_2));
  alu Arithmetic_Logic_Unit (
    .Result(Arithmetic_Logic_Unit_result), .ALUSel(control_logic_1_alusel), .A(multiplexer_3_out),
    .B(multiplexer_4_out));
  // mem_main DMEM: pin names not known; wires that end beside it: Arithmetic_Logic_Unit_result, RegFile_read_data_2, in_2, control_logic_1_memrw, DMEM_p5
  assign bit_extender_1_out = {{16{DMEM_p5[15]}}, DMEM_p5[15:0]};  // Bit_Extender bit_extender_1
  Multiplexer #(.width(32), .enable("false")) multiplexer_5 (
    .in0(DMEM_p5), .in1(bit_extender_2_out), .out(multiplexer_5_out), .sel(control_logic_1_out_14));
  assign bit_extender_2_out = {{24{DMEM_p5[7]}}, DMEM_p5[7:0]};  // Bit_Extender bit_extender_2
  Multiplexer #(.width(32), .enable("false")) multiplexer_6 (
    .in0(multiplexer_5_out), .in1(bit_extender_1_out), .out(multiplexer_6_out), .sel(control_logic_1_out_15));
  Multiplexer #(.select(2), .width(32), .enable("false")) multiplexer_7 (
    .in0(PROGRAM_COUNTER), .in1(Arithmetic_Logic_Unit_result), .in2(multiplexer_6_out), .out(wb),
    .sel(control_logic_1_wbsel));  // open: in3

  // Other names for the same wires on the sheet: clk = in_2

  // Notes on the sheet:
  //   Output
  //   IMEM (do **NOT** move this)
  //   Inputs
  //   Inputs/Outputs for testing. Do **NOT** move these.
endmodule

module swlt (
  input  [31:0] in_1,
  input  [31:0] in_2,
  output out_3
);

  Comparator #(.width(32)) comparator_1 (.a(in_2), .b(in_1), .gt(out_3));  // open: eq, lt

  // Other names for the same wires on the sheet: offset[31:0] = in_2; rs2[31:0] = in_1; swlt = out_3

  // Notes on the sheet:
  //   INPUTS to your circuit
  //   DON'T CHANGE THE LOCATIONS OF THE INPUTS AND OUTPUTS!
  //   OUTPUT from your circuit
endmodule
